// Digital circuit control.dig as structural Verilog
module control (
  input  [6:0] opcode,
  output [1:0] ALUOp,
  output Jalr,
  output ALUSrc,
  output MemtoReg,
  output RegWrite,
  output MemRead,
  output MemWrite,
  output Branch
);

  wire not_1_out;

  not not_1 (not_1_out, opcode[5]);
  not not_2 (MemtoReg, opcode[4]);
  not not_3 (Jalr, opcode[3]);
  or or_1 (ALUSrc, opcode[2], not_1_out);
  and and_1 (Branch, opcode[2], MemtoReg, opcode[5], opcode[6]);

  assign ALUOp = {opcode[5], 1'b0};
  assign MemRead = 1'b1;
  assign MemWrite = 1'b0;
  assign RegWrite = 1'b1;

  // Notes on the sheet:
  //   opcode: 6-0 of the instruction
endmodule
