// Digital circuit cpu.dig as structural Verilog
module cpu (
  input  clk
);

  wire add_1_c_o, control_1_alusrc, control_1_branch, control_1_jalr, control_1_memread, control_1_memtoreg,
       control_1_memwrite, control_1_regwrite, i30, not_1_out;
  wire [1:0] control_1_aluop;
  wire [2:0] funct3;
  wire [3:0] alu_control_1_op;
  wire [4:0] add_1_s, PC_q, rd, rs1;
  wire [6:0] opcode;
  wire [11:0] ITypeImmediate;
  wire [31:0] alu_1_out, bitextender_1_out, multiplexer_1_out, multiplexer_2_out, ramdualport_1_d,
       register_file_1_data1_out, register_file_1_data2_out;

  Register #(.Bits(5), .isProgramCounter("true")) PC (.D(add_1_s), .C(clk), .en(1'b1), .Q(PC_q));
  ROM #(.AddrBits(5), .Bits(32)) rom_1 (
    .A(PC_q), .sel(1'b1), .D({ITypeImmediate[11], i30, ITypeImmediate[9:0], rs1, funct3, rd, opcode}));
  Add #(.Bits(5)) add_1 (.a(PC_q), .b(5'b00001), .c_i(1'b0), .s(add_1_s), .c_o(add_1_c_o));
  // Probe on add_1_c_o
  // Probe on {ITypeImmediate[11], i30, ITypeImmediate[9:0], rs1, funct3, rd, opcode}
  control control_1 (
    .opcode(opcode), .ALUOp(control_1_aluop), .Jalr(control_1_jalr), .ALUSrc(control_1_alusrc),
    .MemtoReg(control_1_memtoreg), .RegWrite(control_1_regwrite), .MemRead(control_1_memread),
    .MemWrite(control_1_memwrite), .Branch(control_1_branch));  // open: PCToReg, CondBranch, UpperImm
  register_file register_file_1 (
    .clk(clk), .read_reg1(rs1), .read_reg2(ITypeImmediate[4:0]), .data_in(multiplexer_2_out), .write_reg(rd),
    .str(control_1_regwrite), .data1_out(register_file_1_data1_out), .data2_out(register_file_1_data2_out));
  BitExtender #(.inputBits(12), .outputBits(32)) bitextender_1 (
    .in({ITypeImmediate[11], i30, ITypeImmediate[9:0]}), .out(bitextender_1_out));
  // Probe on bitextender_1_out
  Multiplexer #(.Bits(32)) multiplexer_1 (
    .sel(control_1_alusrc), .in_0(register_file_1_data2_out), .in_1(bitextender_1_out),
    .out(multiplexer_1_out));
  alu alu_1 (.in_1(register_file_1_data1_out), .in_2(multiplexer_1_out), .operation(alu_control_1_op), .out(alu_1_out));
  alu_control alu_control_1 (.funct3(funct3), .i30(i30), .ALUOp(control_1_aluop), .Op(alu_control_1_op));
  RAMDualPort #(.AddrBits(4), .Bits(32)) ramdualport_1 (
    .A(alu_1_out[3:0]), .Din(register_file_1_data2_out), .str(control_1_memwrite), .C(clk),
    .ld(control_1_memread), .D(ramdualport_1_d));
  Multiplexer #(.Bits(32)) multiplexer_2 (
    .sel(not_1_out), .in_0(ramdualport_1_d), .in_1(alu_1_out), .out(multiplexer_2_out));
  not not_1 (not_1_out, control_1_memtoreg);

  // Other names for the same wires on the sheet: rs2[4:0] = ITypeImmediate[4:0]; ITypeImmediate[10] = i30

  // Notes on the sheet:
  //   clk: Hz: 2147483647
  //   https://msyksphinz-self.github.io/riscv-isadoc/html/rvi.html#lb
  //   contents of rom_1 (hex, n*v repeats v):
  //   1200093,809093,3408093,8113,401101b3,1009213,fff00513,fe5ff06f
endmodule
